# Fritzing sketch dht22 (saved by Fritzing 0.9.2b)
breadboards: 1

parts:
  Raspberry_Pi_1 = Raspberry Pi 3 [part_number=RPI-3-V1.2]
  R1 = Resistor [tolerance=±5% resistance=10k package="0603 [SMD]"]
  RHT1 = Humidity and Temperature Sensor RHT03

nets:
  3V3: Raspberry_Pi_1.3v3, R1.Pin_0, RHT1.Vcc
  N1: Raspberry_Pi_1.GIPO4, R1.Pin_1, RHT1.Data-signal
  N2: Raspberry_Pi_1.GND, RHT1.GND_2
